# Fritzing sketch Untitled Sketch 2 (saved by Fritzing 0.9.3b)
breadboards: 1

parts:
  Parça1 = Arduino Uno (Rev3)
  Parça2 = Bluetooth HC-05 Macho
  LED1 = LED - 5mm [color="Red (633nm)" package="5 mm [THT]"]
  LED2 = LED - 5mm [color="Red (633nm)" package="5 mm [THT]"]
  LED3 = LED - 5mm [color="Red (633nm)" package="5 mm [THT]"]

nets:
  N1: Parça1.D0/RX, Parça2.TXD
  N2: Parça1.D1/TX, Parça2.RXD
  N3: Parça1.D6_PWM, LED1.anode
  N4: Parça1.D7, LED2.anode
  5V: Parça1.5V, Parça2.VCC
  GND: Parça1.GND, Parça2.GND, LED1.cathode, LED2.cathode, LED3.cathode

notes:
  ModülünTX bacağını arduino nun RX bacağına bağladık çünkü haberleşme için karşılıklı pinlerin bağlanması şart
