# Fritzing sketch dht11 (saved by Fritzing 0.9.3b)
breadboards: 1

parts:
  DHT1 = DHT11 Humitidy and Temperature Sensor
  Parça1 = Arduino Uno (Rev3) - ICSP

nets:
  N1: DHT1.VDD, Parça1.D2
  N2: DHT1.DATA, Parça1.5V
  GND: DHT1.GND, Parça1.GND

notes:
  Sinyal
  5v
  GND

custom parts:
  DHT11 Humitidy and Temperature Sensor: DHT11 Humidity and Temperature Sensor
