# Fritzing sketch hareket_Dedektoru (saved by Fritzing 0.9.3b)
breadboards: 1

parts:
  Parça1 = HC-SR501 Body Sensor Module
  Arduino_UNO = Arduino Uno (Rev3)
  J1 = Basic Servo

nets:
  VCC: Parça1.VCC, Arduino_UNO.5V, J1.vcc
  N1: Parça1.OUT, Arduino_UNO.D8
  GND: Parça1.GND, Arduino_UNO.GND, J1.gnd
  N2: Arduino_UNO.D9_PWM, J1.pulse

custom parts:
  HC-SR501 Body Sensor Module: Pyroelectric Infrared PIR Motion Sensor Detector Module
