# Fritzing sketch Untitled Sketch 2 (saved by Fritzing 0.9.3b)
breadboards: 1

parts:
  Parça1 = Arduino Uno (Rev3)
  U1 = TCRT5000 [package=THT]
  R1 = Resistor [tolerance=±5% resistance=220 package=THT]
  R2 = Resistor [tolerance=±5% resistance=220 package=THT]
  R5 = Resistor [tolerance=±5% resistance=4.7k package=THT]
  LED1 = LED - 5mm [color="Red (633nm)" package="5 mm [THT]"]

nets:
  N1: Parça1.A0, Parça1.GND, U1.Pin_1, U1.Pin_2, U1.Pin_3, U1.Pin_4, R1.Pin_0, R5.Pin_1, LED1.cathode
  N2: Parça1.D2, R2.Pin_1
  N3: Parça1.5V, R1.Pin_1, R5.Pin_0
  N4: R2.Pin_0, LED1.anode

custom parts:
  TCRT5000: TCRT5000 optical reflective sensor
