# Fritzing sketch Untitled Sketch 2 (saved by Fritzing 0.9.3b)
breadboards: 1

parts:
  Parça1 = Arduino Uno (Rev3)
  LED1 = RGB LED (com. cathode, rbg) [package="5 mm [THT]"]
  S1 = Pushbutton [package="[THT]"]
  S2 = Pushbutton [package="[THT]"]
  S3 = Pushbutton [package="[THT]"]
  MOTOR3 = 28BYJ-48 Stepper Motor
  X3 = X113647 Stepper Driver Board [package=board]

nets:
  N1: Parça1.A3, LED1.green_anode
  N2: Parça1.A4/SDA, LED1.common_cathode
  N3: Parça1.A5/SCL, LED1.red_anode
  N4: Parça1.D9_PWM, Parça1.D10_PWM/SS, Parça1.D11_PWM/MOSI, Parça1.5V, S1.Pin_3, S1.Pin_4, S2.Pin_3, S2.Pin_4, S3.Pin_3, S3.Pin_4, X3.+V
  N5: Parça1.D2, X3.IN4
  N6: Parça1.D3_PWM, X3.IN3
  N7: Parça1.D4, X3.IN2
  N8: Parça1.D5_PWM, X3.IN1
  GND: Parça1.GND, LED1.blue_anode, S1.Pin_1, S1.Pin_2, S2.Pin_1, S2.Pin_2, S3.Pin_1, S3.Pin_2, X3.GND
  N9: MOTOR3.BLUE, X3.BLUE
  N10: MOTOR3.PINK, X3.PINK
  N11: MOTOR3.RED, X3.RED
  N12: MOTOR3.ORANGE, X3.ORANGE
  N13: MOTOR3.YELLOW, X3.YELLOW

custom parts:
  28BYJ-48 Stepper Motor: 28BYJ-48 gear-reduction stepper motor (small)
  X113647 Stepper Driver Board: A common stepper motor driver board based on ULN2003APG darlington array
