# Fritzing sketch Untitled Sketch 2 (saved by Fritzing 0.9.3b)
breadboards: 1

parts:
  Parça1 = Arduino Uno (Rev3)
  S1 = Pushbutton [package="[THT]"]
  S2 = Pushbutton [package="[THT]"]
  7_Segment1 = 7 Segment Display
  R1 = Resistor [tolerance=±5% resistance=220 package=THT]
  R2 = Resistor [tolerance=±5% resistance=220 package=THT]

nets:
  N1: Parça1.D8, 7_Segment1.Segment_DP
  N2: Parça1.D9_PWM, 7_Segment1.Segment_E
  N3: Parça1.D10_PWM/SS, 7_Segment1.Segment_D
  N4: Parça1.GND, S1.Pin_3, S1.Pin_4, S2.Pin_3, S2.Pin_4, 7_Segment1.common_anode, R1.Pin_0, R2.Pin_0
  N5: Parça1.D2, S1.Pin_1, S1.Pin_2, R1.Pin_1
  N6: Parça1.D3_PWM, 7_Segment1.Segment_F
  N7: Parça1.D4, S2.Pin_1, S2.Pin_2, R2.Pin_1
  N8: Parça1.D5_PWM, 7_Segment1.Segment_G
  N9: Parça1.D6_PWM, 7_Segment1.Segment_B
  N10: Parça1.D7, 7_Segment1.Segment_C
