# Fritzing sketch Untitled Sketch 2 (saved by Fritzing 0.9.3b)
breadboards: 1

parts:
  Parça1 = Arduino Uno (Rev3)
  U2 = GAS_SENSOR [package=mq-3]
  LCD1 = LCD screen
  LCM1602_IIC1 = LCM1602 IIC [part_number="LCM1602 IIC" chip_label="LCM1602 IIC" package="DIP (Dual Inline) [THT]"]

nets:
  N1: Parça1.A0, U2.B1
  N2: Parça1.A4/SDA, LCM1602_IIC1.SDA
  N3: Parça1.A5/SCL, LCM1602_IIC1.SCL
  GND: Parça1.GND, U2.A1, LCM1602_IIC1.GND
  5V: Parça1.5V, LCM1602_IIC1.VCC
  VSS: LCD1.VSS, LCM1602_IIC1.VSS
  VDD: LCD1.VDD, LCM1602_IIC1.VDD
  N4: LCD1.V0, LCM1602_IIC1.V0
  N5: LCD1.RS, LCM1602_IIC1.RS
  N6: LCD1.R/W, LCM1602_IIC1.RW
  N7: LCD1.E, LCM1602_IIC1.E
  N8: LCD1.DB0, LCM1602_IIC1.D0
  N9: LCD1.DB1, LCM1602_IIC1.D1
  N10: LCD1.DB2, LCM1602_IIC1.D2
  N11: LCD1.DB3, LCM1602_IIC1.D3
  N12: LCD1.DB4, LCM1602_IIC1.D4
  N13: LCD1.DB5, LCM1602_IIC1.D5
  N14: LCD1.DB6, LCM1602_IIC1.D6
  N15: LCD1.DB7, LCM1602_IIC1.D7
  N16: LCD1.LED+, LCM1602_IIC1.A
  N17: LCD1.LED-, LCM1602_IIC1.K

custom parts:
  LCM1602 IIC: I2C-Module to use a 1602 or 2004 LCD on with the wire.h libory Serial LCD Modul
