# Fritzing sketch Untitled Sketch 2 (saved by Fritzing 0.9.3b)
breadboards: 1

parts:
  Parça1 = Arduino Uno (Rev3)
  J2 = Basic Servo
  Parça2 = Thumb Joystick
  LED1 = LEDs [package=led10mm]
  LED2 = LEDs [package=led10mm]
  LED3 = LEDs [package=led10mm]
  LED4 = LEDs [package=led10mm]

nets:
  N1: Parça1.A0, Parça2.VERT
  N2: Parça1.A1, Parça2.HORZ
  N3: Parça1.D10_PWM/SS, LED1.A
  N4: Parça1.D11_PWM/MOSI, LED2.A
  N5: Parça1.D12/MISO, LED3.A
  N6: Parça1.D13/SCK, LED4.A
  N7: Parça1.D3_PWM, J2.pulse
  5V: Parça1.5V, J2.vcc, Parça2.SEL
  GND: Parça1.GND, J2.gnd, Parça2.GND

notes:
  5V
  URX
  URY
