# Fritzing sketch lm35 ile sıcaklık ölçümü (saved by Fritzing 0.9.3b)
breadboards: 1

parts:
  Parça1 = Arduino Uno (Rev3)
  Q1 = NPN-Transistor [package="TO92 [THT]"]
  LCD1 = LCD screen
  R1 = Rotary Potentiometer (Small) [maximum_resistance=100kΩ package=THT]

nets:
  N1: Parça1.A0, Q1.B
  N2: Parça1.D12/MISO, LCD1.E
  N3: Parça1.D13/SCK, LCD1.RS
  N4: Parça1.D2, LCD1.DB7
  N5: Parça1.D3_PWM, LCD1.DB6
  N6: Parça1.D4, LCD1.DB5
  N7: Parça1.D5_PWM, LCD1.DB4
  N8: Parça1.3V3, LCD1.LED+
  5V: Parça1.5V, Q1.E, LCD1.VDD, R1.leg1, R1.leg2
  GND: Parça1.GND, Q1.C, LCD1.VSS, LCD1.R/W, LCD1.LED-
  N9: LCD1.V0, R1.wiper
